# Fritzing sketch DRV8833 (saved by Fritzing 0.9.3b)
breadboards: 1

parts:
  Part1 = Arduino Nano (Rev3.0)
  M1 = DC Motor
  M2 = DC Motor
  Part2 = Adafruit DRV8833 DC/Stepper Motor Driver [part_number="Adafruit #3297"]
  NiMH_4_8V = 4 x AAA Battery Mount

nets:
  GND: Part1.GND, Part2.GND, NiMH_4_8V.-
  N1: Part1.D4, Part2.AIN2
  N2: Part1.D5, Part2.AIN1
  N3: Part1.D6, Part2.!SLEEP
  N4: Part1.D7, Part2.BIN1
  N5: Part1.D8, Part2.BIN2
  N6: Part1.5V, Part2.VMOTOR, NiMH_4_8V.+
  N7: M1.pin_1, Part2.BOUT1
  N8: M1.pin_2, Part2.BOUT2
  N9: M2.pin_1, Part2.AOUT1
  N10: M2.pin_2, Part2.AOUT2

custom parts:
  Adafruit DRV8833 DC/Stepper Motor Driver: Spin two DC motors or step one bi-polar or uni-polar stepper with up to 1.2A per channel using the DRV8833. This motor driver chip is a nice alternative to the TB6612 driver. Like that chip, you get 2 full H-bridges, but this chip is better for low voltage uses (can run from 2.7V up to 10.8V motor power) and has built in current limiting capability. We set it up for 1A current limiting so you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
