# Fritzing sketch Wemos-LM35-OLED (saved by Fritzing 0.9.3b)
breadboards: 1

parts:
  WeMos_D1_Mini1 = WeMos D1 Mini  # not connected
  T1 = LM35 Temperature Sensor [package="TO92 [THT]"]
  Squix1 = OLED 0.96" 128x64 I2C SSD1306

nets:
  N1: T1.+Vs, Squix1.VCC
  GND: T1.GND, Squix1.GND
